// Logisim project 4 bit Binary to Gray Code Converter using xor gates.circ as structural Verilog: 1 circuit, main circuit main
module main (
  input  B3,
  input  B2,
  input  B1,
  input  B0,
  output A3,
  output A2,
  output A1,
  output A0
);

  xor xor_1 (A0, B0, B1);
  xor xor_2 (A1, B1, B2);
  xor xor_3 (A2, B2, B3);

  assign A3 = B3;

  // Notes on the sheet:
  //   Binary Inputs:
  //   Gray Code Outputs:
endmodule
