// Logisim project 4 bit binary to gray code converter without xor gates.circ as structural Verilog: 1 circuit, main circuit main
module main (
  input  B3,
  input  B2,
  input  B1,
  input  B0,
  output A3,
  output A2,
  output A1,
  output A0
);

  wire and_1_out, and_2_out, and_3_out, and_4_out, and_5_out, and_6_out, not_1_out, not_2_out, not_3_out,
       not_4_out;

  not not_1 (not_1_out, B0);
  not not_2 (not_2_out, B1);
  and and_1 (and_1_out, not_2_out, B0);
  and and_2 (and_2_out, B1, not_1_out);
  and and_3 (and_3_out, B1, not_3_out);
  and and_4 (and_4_out, not_2_out, B2);
  not not_3 (not_3_out, B2);
  and and_5 (and_5_out, not_3_out, B3);
  and and_6 (and_6_out, B2, not_4_out);
  not not_4 (not_4_out, B3);
  or or_1 (A0, and_2_out, and_1_out);
  or or_2 (A1, and_3_out, and_4_out);
  or or_3 (A2, and_6_out, and_5_out);

  assign A3 = B3;
endmodule
