// Logisim project 4 bit decimal to gray code converter.circ as structural Verilog: 1 circuit, main circuit main
module main (
  input  _0,
  input  _1,
  input  _2,
  input  _3,
  input  _4,
  input  _5,
  input  _6,
  input  _7,
  input  _8,
  input  _9,
  input  _10,
  input  _11,
  input  _12,
  input  _13,
  input  _14,
  input  _15,
  output A0,
  output A1,
  output A2,
  output A3
);

  wire x1_out, x2_out, x3_out, x4_out, x5_out;

  or x1 (x1_out, _4, _5);
  or x2 (x2_out, _8, _9);
  or x3 (x3_out, _10, _11);
  or x4 (x4_out, _12, _13);
  or x5 (x5_out, x2_out, x3_out);
  or or_1 (A0, _14, _13, _10, _9, _6, _5, _2, _1);
  or or_2 (A1, _2, _3, x4_out, x1_out, x3_out);
  or or_3 (A2, _6, _7, x1_out, x5_out);
  or or_4 (A3, _14, x5_out, _15, x4_out);

  // Notes on the sheet:
  //   Decimal Values
  //   Gray Codes
endmodule
