// Logisim project artitrary counter 0-2-4-5-7.circ as structural Verilog: 1 circuit, main circuit main
module main (
  input  in_1,
  output C,
  output B,
  output A
);

  wire A_qn, button_1_out, or_1_out;

  or or_1 (or_1_out, C, A_qn);
  Button button_1 (.out(button_1_out));
  J_K_Flip_Flop u_C (.J(A), .clk(button_1_out), .K(B), .Q(C));  // open: Qn, preset, en, reset
  J_K_Flip_Flop u_B (.J(or_1_out), .clk(button_1_out), .K(in_1), .Q(B));  // open: Qn, preset, en, reset
  J_K_Flip_Flop u_A (.J(B), .clk(button_1_out), .K(B), .Q(A), .Qn(A_qn));  // open: preset, en, reset
endmodule
